# Fritzing sketch strix-takeover-breadboard (saved by Fritzing 1.0.3)
breadboards: 1

parts:
  Nano1 = Arduino Nano (Rev3.0)
  R1 = Resistor [resistance=4.7kΩ package=THT]
  C1 = Ceramic Capacitor [capacitance=1µF package="100 mil [THT, multilayer]"]
  R2 = Resistor [resistance=4.7kΩ package=THT]
  C2 = Ceramic Capacitor [capacitance=1µF package="100 mil [THT, multilayer]"]

nets:
  N1: Nano1.GND, C1.1, C2.1
  N2: Nano1.D9, R1.Pin_0
  N3: Nano1.D10, R2.Pin_0
  N4: R1.Pin_1, C1.0
  N5: R2.Pin_1, C2.0

notes:
  STRIX - controller takeover, Variant B (PWM wiper synthesis)
  The Nano synthesizes the two wiper voltages that the handheld
  controller's trigger and steering pots used to produce. Each
  channel is a 4.7k + 1uF RC low-pass filter on a Timer1 PWM pin.
  D9 = throttle, D10 = steering, A0 = controller rail sense.
  ORANGE (A0): to the controller's pot HIGH / rail pin.
  Scales every duty to the sagging AA rail so calibrated
  neutral cannot drift. Do not omit this wire.
  Nano is rotated so the USB end faces the board edge; the
  phone's OTG cable exits left and powers the Nano.
  BLUE -> controller TRIGGER pot WIPER pin
  GREEN -> controller WHEEL pot WIPER pin
  BLACK -> controller GROUND (pot LOW pin)
  Identify which harness wire is the wiper before cutting:
  see docs/pot-identification.md. On this build's Hosim
  controller the BLACK harness wire was the wiper.
  Distance sensors (HC-SR04 x2 on D2-D5, VL53L4CD on A4/A5
  via a 3.3V level shifter) are documented separately in
  docs/sensor-wiring.md and are not shown here.
